# Fritzing sketch Agitator (saved by Fritzing 0.9.0b)
breadboards: 1

parts:
  R1 = Resistor [tolerance=±5% resistance=220 package=THT]  # not connected
  R2 = Resistor [tolerance=±5% resistance=220 package=THT]  # not connected
  R3 = Resistor [tolerance=±5% resistance=1k package=THT]
  R4 = Resistor [tolerance=±5% resistance=1k package=THT]
  R5 = Slide Potentiometer [maximum_resistance=100kΩ]  # not connected
  R6 = Slide Potentiometer [maximum_resistance=100kΩ]  # not connected
  LED1 = LED - 5mm [color="Red (633nm)" package="5 mm [THT]"]
  LED2 = LED - 5mm [color="Red (633nm)" package="5 mm [THT]"]
  IC1 = L293D [package=THT]  # not connected
  U1 = SWITCH-SPST-2 [package=switch-spst-vertical]
  U2 = SWITCH-SPST-2 [package=switch-spst-vertical]
  Part2 = Arduino Uno (Rev3)
  M1 = Stepper Motor - Bipolar  # not connected

nets:
  N1: R3.Pin_0, LED2.anode
  N2: R3.Pin_1, U2.O
  N3: R4.Pin_0, LED1.anode
  N4: R4.Pin_1, U1.O
  N5: LED1.cathode, LED2.cathode
  N6: U1.P, U2.P, Part2.5V
